// Logisim project Ex15.circ as structural Verilog: 1 circuit, main circuit main
module main (
  input  I0,
  input  C0,
  input  C1,
  output out_4,
  output out_5
);

  wire and_1_out, and_2_out, and_4_out, and_5_out, clock_1_out, not_1_out, not_2_out, or_1_out, or_2_out;

  Clock clock_1 (.out(clock_1_out));
  not not_1 (not_1_out, C0);
  not not_2 (not_2_out, C1);
  and and_1 (and_1_out, not_1_out, C1);
  and and_2 (and_2_out, C0, not_2_out);
  // AND_Gate and_3 has open pins: in0=C0, in1=C1, out=open
  and and_4 (and_4_out, and_2_out, clock_1_out);
  and and_5 (and_5_out, and_1_out, clock_1_out);
  buf or_1 (or_1_out, and_4_out);  // OR_Gate
  buf or_2 (or_2_out, and_5_out);  // OR_Gate
  Register #(.width(1)) RA (.D(I0), .Q(out_4), .clk(or_1_out));  // open: en, clr
  Register #(.width(1)) RB (.D(I0), .Q(out_5), .clk(or_2_out));  // open: en, clr
endmodule
