// Logisim project Ex16.circ as structural Verilog: 1 circuit, main circuit main
module main (
  input  [1:0] I0,
  input  C0,
  input  C1,
  output [1:0] out_4,
  output [1:0] out_5,
  output [1:0] out_6
);

  wire and_1_out, and_2_out, and_3_out, and_4_out, and_5_out, and_6_out, clock_1_out, not_1_out, not_2_out,
       not_3_out, not_4_out, not_5_out;

  Clock clock_1 (.out(clock_1_out));
  not not_1 (not_1_out, C0);
  not not_2 (not_2_out, C1);
  and and_1 (and_1_out, not_1_out, C1);
  and and_2 (and_2_out, C0, not_2_out);
  and and_3 (and_3_out, C0, C1);
  not not_3 (not_3_out, and_3_out);
  not not_4 (not_4_out, and_2_out);
  not not_5 (not_5_out, and_1_out);
  and and_4 (and_4_out, and_1_out, clock_1_out);
  and and_5 (and_5_out, not_3_out, not_4_out, clock_1_out, not_5_out);
  and and_6 (and_6_out, and_2_out, clock_1_out);
  Subtractor #(.width(2)) subtractor_1 (.a(out_5), .b(out_4), .out(out_6), .bin(and_6_out));  // open: bout
  Register #(.width(2)) R0 (.D(I0), .Q(out_4), .clk(and_5_out));  // open: en, clr
  Register #(.width(2)) R1 (.D(I0), .Q(out_5), .clk(and_4_out));  // open: en, clr
  Register #(.width(2)) R2 ();  // open: D, en, Q, clk, clr
endmodule
